// Digital circuit Ejercicio5.dig as structural Verilog
module Ejercicio5 (
  input  i0,
  input  i1,
  input  i2,
  input  i3
);

  wire a, b, c, d, e, f, g, ii0, ii1, ii2, ii3, nand_1_out, nand_2_out, nand_3_out, nand_4_out, nand_5_out,
       nand_6_out, nand_7_out, nand_8_out, nand_9_out, nand_10_out, nand_11_out, nand_12_out, nand_13_out,
       nand_14_out, nand_15_out, nand_17_out, nand_18_out, nand_19_out, nand_26_out, nand_27_out,
       nand_28_out, nand_29_out, nand_30_out, nand_31_out, nand_34_out, nand_35_out, nand_36_out,
       nand_37_out, nand_38_out, nand_39_out, nand_40_out, nand_41_out, nand_42_out;

  nand nand_1 (nand_1_out, i2, i2);
  nand nand_2 (nand_2_out, i0, i0);
  nand nand_3 (nand_3_out, i1, i1);
  nand nand_4 (nand_4_out, i0, i0);
  nand nand_5 (nand_5_out, i1, i0);
  nand nand_6 (nand_6_out, nand_3_out, nand_4_out);
  nand nand_7 (nand_7_out, i2, i0);
  nand nand_8 (nand_8_out, nand_1_out, nand_2_out);
  nand nand_9 (nand_9_out, nand_5_out, nand_6_out);
  nand nand_10 (nand_10_out, nand_7_out, nand_8_out);
  nand nand_11 (nand_11_out, ii2, ii2);
  nand nand_12 (nand_12_out, nand_9_out, nand_9_out);
  nand nand_13 (nand_13_out, i3, i3);
  nand nand_14 (nand_14_out, i1, i1);
  nand nand_15 (nand_15_out, nand_10_out, nand_10_out);
  nand nand_16 (b, nand_11_out, nand_12_out);
  nand nand_17 (nand_17_out, i2, i2);
  nand nand_18 (nand_18_out, ii1, ii1);
  nand nand_19 (nand_19_out, i0, i0);
  nand nand_20 (a, nand_13_out, nand_14_out, nand_15_out);
  nand nand_21 (c, nand_17_out, nand_18_out, nand_19_out);
  nand nand_22 (ii3, i3, i3);
  nand nand_23 (ii2, i2, i2);
  nand nand_24 (ii1, i1, i1);
  nand nand_25 (ii0, i0, i0);
  nand nand_26 (nand_26_out, ii0, i1);
  nand nand_27 (nand_27_out, ii0, ii2);
  Seven_Seg seven_seg_1 (.a(a), .b(b), .c(c), .d(d), .e(e), .f(f), .g(g), .dp(1'b0));
  nand nand_28 (nand_28_out, ii0, i1);
  nand nand_29 (nand_29_out, ii0, ii2);
  nand nand_30 (nand_30_out, ii2, i1);
  nand nand_31 (nand_31_out, i2, ii1, i0);
  nand nand_32 (e, nand_26_out, nand_27_out);
  nand nand_33 (d, nand_28_out, nand_29_out, nand_30_out, nand_31_out);
  nand nand_34 (nand_34_out, i2, i2);
  nand nand_35 (nand_35_out, i1, i1);
  nand nand_36 (nand_36_out, i2, i1);
  nand nand_37 (nand_37_out, nand_34_out, nand_35_out);
  nand nand_38 (nand_38_out, ii0, i1);
  nand nand_39 (nand_39_out, ii1, i2);
  nand nand_40 (nand_40_out, i2, ii0);
  nand nand_41 (nand_41_out, ii1, ii0);
  nand nand_42 (nand_42_out, nand_36_out, nand_37_out);
  nand nand_43 (f, ii3, nand_39_out, nand_40_out, nand_41_out);
  nand nand_44 (g, nand_42_out, nand_38_out, ii3);
endmodule
