// Digital circuit NAND.dig as structural Verilog
module NAND (
  input  B,
  input  A,
  output \output 
);

  wire nfet_1_s;

  PFET pfet_1 (.G(A), .S(1'b1), .D(\output ));
  NFET nfet_1 (.G(B), .D(\output ), .S(nfet_1_s));
  NFET nfet_2 (.G(A), .D(nfet_1_s), .S(1'b0));
  PFET pfet_2 (.G(B), .S(1'b1), .D(\output ));

  // Other names for the same wires on the sheet: input_A = A; input_B = B
endmodule
