// Digital circuit NAND3.dig as structural Verilog
module NAND3 (
  input  C,
  input  B,
  input  A,
  output \output 
);

  wire input_1, input_2, nfet_1_s, nfet_3_s, nfet_5_s;

  PFET pfet_1 (.G(A), .S(1'b1), .D(input_1));
  NFET nfet_1 (.G(B), .D(input_1), .S(nfet_1_s));
  NFET nfet_2 (.G(A), .D(nfet_1_s), .S(1'b0));
  PFET pfet_2 (.G(B), .S(1'b1), .D(input_1));
  PFET pfet_3 (.G(C), .S(1'b1), .D(\output ));
  NFET nfet_3 (.G(C), .D(\output ), .S(nfet_3_s));
  NFET nfet_4 (.G(input_2), .D(nfet_3_s), .S(1'b0));
  PFET pfet_4 (.G(input_1), .S(1'b1), .D(input_2));
  PFET pfet_5 (.G(input_2), .S(1'b1), .D(\output ));
  NFET nfet_5 (.G(input_1), .D(input_2), .S(nfet_5_s));
  NFET nfet_6 (.G(input_1), .D(nfet_5_s), .S(1'b0));
  PFET pfet_6 (.G(input_1), .S(1'b1), .D(input_2));

  // Other names for the same wires on the sheet: input_A = A; input_B = B; input_C = C
endmodule
