// Digital circuit NAND3Tran.dig as structural Verilog
module NAND3Tran (
  input  A,
  input  B,
  input  C,
  output Output
);

  wire fgnfet_1_s, fgnfet_2_s;

  FGPFET fgpfet_1 (.G(A), .S(1'b1), .D(Output));
  FGPFET fgpfet_2 (.G(B), .S(1'b1), .D(Output));
  FGPFET fgpfet_3 (.G(C), .S(1'b1), .D(Output));
  FGNFET fgnfet_1 (.G(C), .D(Output), .S(fgnfet_1_s));
  FGNFET fgnfet_2 (.G(B), .D(fgnfet_1_s), .S(fgnfet_2_s));
  FGNFET fgnfet_3 (.G(A), .D(fgnfet_2_s), .S(1'b0));
endmodule
