// Digital circuit OR.dig as structural Verilog
module OR (
  input  A,
  input  B,
  output \output 
);

  wire nfet_1_s, nfet_3_s, nfet_5_s, output_A, output_B;

  PFET pfet_1 (.G(A), .S(1'b1), .D(output_A));
  NFET nfet_1 (.G(A), .D(output_A), .S(nfet_1_s));
  NFET nfet_2 (.G(A), .D(nfet_1_s), .S(1'b0));
  PFET pfet_2 (.G(B), .S(1'b1), .D(output_B));
  PFET pfet_3 (.G(A), .S(1'b1), .D(output_A));
  NFET nfet_3 (.G(B), .D(output_B), .S(nfet_3_s));
  NFET nfet_4 (.G(B), .D(nfet_3_s), .S(1'b0));
  PFET pfet_4 (.G(B), .S(1'b1), .D(output_B));
  PFET pfet_5 (.G(output_A), .S(1'b1), .D(\output ));
  NFET nfet_5 (.G(output_B), .D(\output ), .S(nfet_5_s));
  NFET nfet_6 (.G(output_A), .D(nfet_5_s), .S(1'b0));
  PFET pfet_6 (.G(output_B), .S(1'b1), .D(\output ));

  // Other names for the same wires on the sheet: input_A = A; input_B = B
endmodule
