// Digital circuit Punto3Pag1.dig as structural Verilog
module Punto3Pag1 (
  input  X,
  input  Y,
  input  Z,
  output Output
);

  wire nand_3_out, nand_4_out, nand_5_out, nand_6_out, nand_7_out, nand_8_out, Xx, Yy;

  nand nand_1 (Yy, Y, Y, Y);
  nand nand_2 (Xx, X, X, X);
  nand nand_3 (nand_3_out, Xx, Yy, Z);
  nand nand_4 (nand_4_out, Xx, Y, Z);
  nand nand_5 (nand_5_out, X, Yy, Z);
  nand nand_6 (nand_6_out, X, X, Y);
  nand nand_7 (nand_7_out, nand_3_out, nand_4_out, nand_5_out);
  nand nand_8 (nand_8_out, nand_7_out, nand_7_out, nand_7_out);
  nand nand_9 (Output, nand_8_out, nand_8_out, nand_6_out);
endmodule
