// Digital circuit Punto4.dig as structural Verilog
module Punto4 (
  input  x,
  input  y,
  output XOR,
  output XORC,
  output XORN
);

  wire nand_1_out, nand_2_out, nand_3_out, nand_4_out, nand_5_out, nand_6_out, or_1_out;

  xor xor_1 (XOR, y, x);
  nand nand_1 (nand_1_out, x, x);
  nand nand_2 (nand_2_out, y, y);
  nand nand_3 (nand_3_out, y, x);
  nand nand_4 (nand_4_out, y, x);
  nand nand_5 (nand_5_out, nand_1_out, nand_2_out);
  or or_1 (or_1_out, y, x);
  and and_1 (XORC, nand_3_out, or_1_out);
  nand nand_6 (nand_6_out, nand_4_out, nand_5_out);
  nand nand_7 (XORN, nand_6_out, nand_6_out);
endmodule
