// Digital circuit Ejercicio2.dig as structural Verilog
module Ejercicio2 (
  input  a,
  input  b,
  input  c,
  output S2
);

  wire and_1_out, and_2_out, and_3_out, not_1_out, not_2_out, or_1_out;

  not not_1 (not_1_out, c);
  and and_1 (and_1_out, not_1_out, b);
  not not_2 (not_2_out, b);
  and and_2 (and_2_out, not_2_out, c);
  and and_3 (and_3_out, b, c);
  or or_1 (or_1_out, and_2_out, and_1_out, and_3_out);
  and and_4 (S2, a, or_1_out);
endmodule
