// Digital circuit FlipFlopD_asincrono.dig as structural Verilog
module FlipFlopD_asincrono (
  input  Set,
  input  D,
  input  Clock,
  input  Clear,
  output out_5
);

  wire nand_1_out, nand_2_out, nand_3_out, nand_4_out, nand_5_out, nand_6_out, nand_8_out, not_1_out,
       not_2_out;

  not not_1 (not_1_out, D);
  nand nand_1 (nand_1_out, D, Clock);
  nand nand_2 (nand_2_out, Clock, not_1_out);
  nand nand_3 (nand_3_out, Set, nand_1_out, nand_4_out);
  nand nand_4 (nand_4_out, nand_3_out, nand_2_out, Clear);
  not not_2 (not_2_out, nand_3_out);
  nand nand_5 (nand_5_out, nand_3_out, Clock);
  nand nand_6 (nand_6_out, Clock, not_2_out);
  nand nand_7 (out_5, Set, nand_5_out, nand_8_out);
  nand nand_8 (nand_8_out, out_5, nand_6_out, Clear);
endmodule
