// Digital circuit FlipFlopD_asincrono_En.dig as structural Verilog
module FlipFlopD_asincrono_En (
  input  S,
  input  En,
  input  Clock,
  input  C,
  input  D,
  output Output
);

  wire Dd;

  Multiplexer multiplexer_1 (.sel(En), .in_0(Output), .in_1(D), .out(Dd));
  D_FF_AS d_ff_as_1 (.Set(S), .D(Dd), .C(Clock), .Clr(C), .Q(Output));  // open: nQ
endmodule
