// Digital circuit FlipFlopD_asincrono_En4.dig as structural Verilog
module FlipFlopD_asincrono_En4 (
  input  S,
  input  En,
  input  Clock,
  input  C,
  input  D1,
  input  D2,
  input  D3,
  input  D4,
  output Output1,
  output Output2,
  output Output3,
  output Output4
);

  wire Dd1, Dd2, Dd3, Dd4;

  D_FF_AS d_ff_as_1 (.Set(S), .D(Dd1), .C(Clock), .Clr(C), .Q(Output1));  // open: nQ
  Multiplexer multiplexer_1 (.sel(En), .in_0(Output1), .in_1(D1), .out(Dd1));
  Multiplexer multiplexer_2 (.sel(En), .in_0(Output2), .in_1(D2), .out(Dd2));
  D_FF_AS d_ff_as_2 (.Set(S), .D(Dd2), .C(Clock), .Clr(C), .Q(Output2));  // open: nQ
  Multiplexer multiplexer_3 (.sel(En), .in_0(Output3), .in_1(D3), .out(Dd3));
  D_FF_AS d_ff_as_3 (.Set(S), .D(Dd3), .C(Clock), .Clr(C), .Q(Output3));  // open: nQ
  D_FF_AS d_ff_as_4 (.Set(S), .D(Dd4), .C(Clock), .Clr(C), .Q(Output4));  // open: nQ
  Multiplexer multiplexer_4 (.sel(En), .in_0(Output4), .in_1(D4), .out(Dd4));
endmodule
