// Digital circuit Inverter.dig as structural Verilog
module Inverter (
  input  A,
  output \output 
);

  wire nfet_1_s;

  PFET pfet_1 (.G(A), .S(1'b1), .D(\output ));
  NFET nfet_1 (.G(A), .D(\output ), .S(nfet_1_s));
  NFET nfet_2 (.G(A), .D(nfet_1_s), .S(1'b0));
  PFET pfet_2 (.G(A), .S(1'b1), .D(\output ));

  // Other names for the same wires on the sheet: input_A = A
endmodule
