// Digital circuit Ejericico1.dig as structural Verilog
module Ejericico1 (
  input  D,
  input  V,
  input  M,
  output S,
  output S2
);

  wire and_2_out, and_3_out, and_4_out, not_1_out, not_2_out, or_1_out, or_2_out;

  or or_1 (or_1_out, V, D);
  and and_1 (S, M, or_1_out);
  not not_1 (not_1_out, D);
  not not_2 (not_2_out, V);
  and and_2 (and_2_out, not_2_out, D);
  and and_3 (and_3_out, not_1_out, V);
  and and_4 (and_4_out, D, V);
  or or_2 (or_2_out, and_2_out, and_3_out, and_4_out);
  and and_5 (S2, M, or_2_out);
endmodule
