// Digital circuit Demux.dig as structural Verilog
module Demux (
  input  Sel2,
  input  Sel1,
  input  In,
  output Output
);

  wire and_1_out, and_2_out, and_3_out, and_4_out, not_1_out, not_2_out;

  not not_1 (not_1_out, Sel1);
  not not_2 (not_2_out, Sel2);
  and and_1 (and_1_out, In, not_1_out, not_2_out);
  and and_2 (and_2_out, In, not_2_out, Sel1);
  and and_3 (and_3_out, In, Sel2, not_1_out);
  and and_4 (and_4_out, In, Sel2, Sel1);
  or or_1 (Output, and_1_out, and_2_out, and_3_out, and_4_out);
endmodule
