// Digital circuit JKFlipFLop.dig as structural Verilog
module JKFlipFLop (
  input  J,
  input  K,
  input  Clock,
  output Q,
  output Q_2,
  output Q_3
);

  wire nand_1_out, nand_2_out;

  nand nand_1 (nand_1_out, J, Q_2, Clock);
  nand nand_2 (nand_2_out, Clock, Q, K);
  JK_FF jk_ff_1 (.J(J), .C(Clock), .K(K), .Q(Q_3));  // open: nQ
  nand nand_3 (Q, nand_1_out, Q_2);
  nand nand_4 (Q_2, Q, nand_2_out);

  // Notes on the sheet:
  //   El cambio en Q viene dado cuando Clock
  //   se encuentra activo y alguna de las opciones
  //   J(1) y K(0) también, a diferencia del RS no permite
  //   tener en true  a la vez a Q y Q', pero al tener ambas
  //   opcines encendidas a la vez el circuito tiende a 
  //   oscilar de un valor al otro, por lo que la simulación 
  //   falla.
endmodule
