// Digital circuit Multiplexor8Pines.dig as structural Verilog
module Multiplexor8Pines (
  input  Sel3,
  input  Sel2,
  input  Sel1,
  input  D1,
  input  D2,
  input  D3,
  input  D4,
  input  D5,
  input  D6,
  input  D8,
  input  D7,
  output Output
);

  wire and_1_out, and_2_out, and_4_out, and_5_out, and_6_out, and_7_out, and_8_out, not_1_out, not_2_out,
       not_3_out, or_1_out, or_2_out;

  not not_1 (not_1_out, Sel1);
  not not_2 (not_2_out, Sel2);
  not not_3 (not_3_out, Sel3);
  and and_1 (and_1_out, not_1_out, not_2_out, not_3_out, D1);
  and and_2 (and_2_out, Sel1, not_3_out, not_2_out, D2);
  // And and_3 has open pins: In_1=Sel2, In_2=not_1_out, In_3=not_3_out, In_4=D3, out=open
  and and_4 (and_4_out, Sel3, not_2_out, not_1_out, D4);
  and and_5 (and_5_out, Sel1, Sel2, not_3_out, D5);
  and and_6 (and_6_out, Sel1, not_2_out, Sel3, D6);
  and and_7 (and_7_out, Sel1, Sel2, Sel3, D8);
  and and_8 (and_8_out, Sel3, Sel2, not_1_out, D7);
  or or_1 (or_1_out, and_1_out, and_2_out, and_4_out, and_5_out);
  or or_2 (or_2_out, and_6_out, and_7_out, and_8_out);
  or or_3 (Output, or_1_out, or_2_out);
endmodule
