// Digital circuit Punto4.dig as structural Verilog
module Punto4 (
  input  SConfig,
  input  EnConfig,
  input  CConfig,
  input  DIO1,
  input  DIO2,
  input  DIO1_2,
  input  DIO4,
  input  SEntrada,
  input  CEntrada,
  input  EIO1,
  input  EIO2,
  input  EIO3,
  input  EIO4,
  input  SSalida,
  input  CSalida,
  input  SIO1,
  input  SIO2,
  input  SIO3,
  input  SIO4,
  input  clk,
  output IO1,
  output IO2,
  output IO3,
  output IO4,
  output SEIO1,
  output SEIO2,
  output SEIO3,
  output SEIO4,
  output SSIO1,
  output SSIO2,
  output SSIO3,
  output SSIO4
);

  wire Dd1, Dd2, Dd3, Dd4, Ed1, Ed2, Ed3, Ed4, not_1_out, not_2_out, not_3_out, not_4_out, Ss1, Ss2, Ss3, Ss4;

  D_FF_AS d_ff_as_1 (.Set(SConfig), .D(Dd1), .C(clk), .Clr(CConfig), .Q(IO1));  // open: nQ
  D_FF_AS d_ff_as_2 (.Set(SEntrada), .D(Ed1), .C(clk), .Clr(CEntrada), .Q(SEIO1));  // open: nQ
  D_FF_AS d_ff_as_3 (.Set(SEntrada), .D(Ss1), .C(clk), .Clr(CSalida), .Q(SSIO1));  // open: nQ
  Multiplexer multiplexer_1 (.sel(EnConfig), .in_0(IO1), .in_1(DIO1), .out(Dd1));
  Multiplexer multiplexer_2 (.sel(IO1), .in_0(SEIO1), .in_1(EIO1), .out(Ed1));
  Multiplexer multiplexer_3 (.sel(not_1_out), .in_0(SSIO1), .in_1(SIO1), .out(Ss1));
  not not_1 (not_1_out, IO1);
  Multiplexer multiplexer_4 (.sel(EnConfig), .in_0(IO2), .in_1(DIO2), .out(Dd2));
  D_FF_AS d_ff_as_4 (.Set(SConfig), .D(Dd2), .C(clk), .Clr(CConfig), .Q(IO2));  // open: nQ
  Multiplexer multiplexer_5 (.sel(IO2), .in_0(SEIO2), .in_1(EIO2), .out(Ed2));
  D_FF_AS d_ff_as_5 (.Set(SEntrada), .D(Ed2), .C(clk), .Clr(CEntrada), .Q(SEIO2));  // open: nQ
  Multiplexer multiplexer_6 (.sel(not_2_out), .in_0(SSIO2), .in_1(SIO2), .out(Ss2));
  D_FF_AS d_ff_as_6 (.Set(SEntrada), .D(Ss2), .C(clk), .Clr(CSalida), .Q(SSIO2));  // open: nQ
  not not_2 (not_2_out, IO2);
  Multiplexer multiplexer_7 (.sel(EnConfig), .in_0(IO3), .in_1(DIO1_2), .out(Dd3));
  D_FF_AS d_ff_as_7 (.Set(SConfig), .D(Dd3), .C(clk), .Clr(CConfig), .Q(IO3));  // open: nQ
  Multiplexer multiplexer_8 (.sel(IO3), .in_0(SEIO3), .in_1(EIO3), .out(Ed3));
  D_FF_AS d_ff_as_8 (.Set(SEntrada), .D(Ed3), .C(clk), .Clr(CEntrada), .Q(SEIO3));  // open: nQ
  Multiplexer multiplexer_9 (.sel(not_3_out), .in_0(SSIO3), .in_1(SIO3), .out(Ss3));
  not not_3 (not_3_out, IO3);
  D_FF_AS d_ff_as_9 (.Set(SEntrada), .D(Ss3), .C(clk), .Clr(CSalida), .Q(SSIO3));  // open: nQ
  D_FF_AS d_ff_as_10 (.Set(SConfig), .D(Dd4), .C(clk), .Clr(CConfig), .Q(IO4));  // open: nQ
  D_FF_AS d_ff_as_11 (.Set(SEntrada), .D(Ed4), .C(clk), .Clr(CEntrada), .Q(SEIO4));  // open: nQ
  D_FF_AS d_ff_as_12 (.Set(SEntrada), .D(Ss4), .C(clk), .Clr(CSalida), .Q(SSIO4));  // open: nQ
  Multiplexer multiplexer_10 (.sel(EnConfig), .in_0(IO4), .in_1(DIO4), .out(Dd4));
  Multiplexer multiplexer_11 (.sel(IO4), .in_0(SEIO4), .in_1(EIO4), .out(Ed4));
  Multiplexer multiplexer_12 (.sel(not_4_out), .in_0(SSIO4), .in_1(SIO4), .out(Ss4));
  not not_4 (not_4_out, IO4);

  assign SSalida = SEntrada;

  // Other names for the same wires on the sheet: CC = CConfig; CE = CEntrada; Clock = clk; CS = CSalida;
  //   DIO3 = DIO1_2; EnC = EnConfig; SC = SConfig; SE = SEntrada

  // Notes on the sheet:
  //   Registro de Configuración
  //   DIOX: Configuración I/O numero X.
  //   Entrada 1, Salida 0
  //   Registro de Entradas
  //   EIOX : Entrada I/O numero X
  //   Registro de Salidas
  //   SOX : Salida I/O numero X
endmodule
