// Digital circuit Punto2Demux4Salidas.dig as structural Verilog
module Punto2Demux4Salidas (
  input  Sel2,
  input  Sel1,
  input  In,
  output Output1,
  output Output2,
  output Output3,
  output Output4
);

  wire not_1_out, not_2_out;

  not not_1 (not_1_out, Sel1);
  not not_2 (not_2_out, Sel2);
  and and_1 (Output1, In, not_1_out, not_2_out);
  and and_2 (Output2, In, not_2_out, Sel1);
  and and_3 (Output3, In, Sel2, not_1_out);
  and and_4 (Output4, In, Sel2, Sel1);

  // Notes on the sheet:
  //   Tabla
  //   S1 | S2 | Out |
  //    0 | 0 | Out1 |
  //    1 | 0 | Out2 |
  //    0 | 1 | Out3 |
  //    1 | 1 | Out4 |
endmodule
