// Digital circuit Punto3aFlipFlopRS.dig as structural Verilog
module Punto3aFlipFlopRS (
  input  S,
  input  R,
  input  Clock,
  output Q,
  output Q_2,
  output nQ
);

  wire nand_1_out, nand_2_out;

  nand nand_1 (nand_1_out, S, Clock);
  nand nand_2 (nand_2_out, Clock, R);
  nand nand_3 (Q_2, nand_1_out, nQ);
  nand nand_4 (nQ, Q_2, nand_2_out);
  RS_FF rs_ff_1 (.S(S), .C(Clock), .R(R), .Q(Q));  // open: nQ

  // Notes on the sheet:
  //   Condiciones
  //   El funcionamiento consiste primeramente en la situación donde las salidas
  //   Q y ~Q se retroalimentan logrando un valor constante, ya que siempre que
  //   el clock esté desactivado, una de las entradas de los NANDs finales siempre
  //   será positiva, logrando mantener esos valores con la retroalimentación
  //   antes mencionada. Por otra parte cuando se da la activación del clock permite
  //   que los parámetros S y R tengan un efecto en el circuito, con S se conseguirá 
  //   Q = 1 y ~Q = 0, con R se obtendrá el comportamiento espejo.
  //   El problema de este flip flop se da cuando primero se activan todos los parámetros 
  //   haciendo que Q y ~Q tengan el valor 1, luego al desactivar el clock se genera
  //   una “carrera” entre Q y ~Q para ver cuál cambia primero su valor a 0, 
  //   lo cual genera que el circuito empiece a oscilar.
  //   FlipFlopRS
  //   Circuito de referencia
endmodule
