// Digital circuit Punto4ModeloPinesIO.dig as structural Verilog
module Punto4ModeloPinesIO (
  input  SConfig,
  input  EnConfig,
  input  CConfig,
  input  EnConfigIO1,
  input  SEntrada,
  input  CEntrada,
  input  SSalida,
  input  CSalida,
  input  DatoSalida1,
  input  DatoSalida2,
  input  DatoSalida2_2,
  input  DatoSalida14,
  input  EnableEntradaSalida,
  input  InputIO1,
  input  EnConfigIO2,
  input  EnConfigIO3,
  input  EnConfigIO4,
  input  InputIO2,
  input  InputIO3,
  input  InputIO4,
  input  Clock,
  output SaConfigIO1,
  output RegistroEntrada1,
  output OutputIO1,
  output SaConfigIO2,
  output SaConfigIO3,
  output SaConfigIO4,
  output RegistroEntrada2,
  output RegistroEntrada3,
  output RegistroEntrada4,
  output OutputIO2,
  output OutputIO3,
  output OutputIO4
);

  wire InputIO1_t, InputIO2_t, InputIO3_t, InputIO4_t, multiplexer_1_out, multiplexer_2_out,
       multiplexer_3_out, multiplexer_4_out, multiplexer_5_out, multiplexer_6_out, multiplexer_7_out,
       multiplexer_8_out, multiplexer_9_out, multiplexer_10_out, multiplexer_11_out, multiplexer_12_out,
       OutputIO1_t, OutputIO2_t, OutputIO3_t, OutputIO4_t;

  assign InputIO1_t = ~SaConfigIO1 ? InputIO1 : 1'bz;  // DriverInvSel driverinvsel_1
  assign OutputIO1 = SaConfigIO1 ? OutputIO1_t : 1'bz;  // Driver driver_1
  assign InputIO2_t = ~SaConfigIO2 ? InputIO2 : 1'bz;  // DriverInvSel driverinvsel_2
  assign OutputIO2 = SaConfigIO2 ? OutputIO2_t : 1'bz;  // Driver driver_2
  assign InputIO3_t = ~SaConfigIO3 ? InputIO3 : 1'bz;  // DriverInvSel driverinvsel_3
  assign OutputIO3 = SaConfigIO3 ? OutputIO3_t : 1'bz;  // Driver driver_3
  assign InputIO4_t = ~SaConfigIO4 ? InputIO4 : 1'bz;  // DriverInvSel driverinvsel_4
  assign OutputIO4 = SaConfigIO4 ? OutputIO4_t : 1'bz;  // Driver driver_4
  Multiplexer multiplexer_1 (.sel(EnConfig), .in_0(SaConfigIO1), .in_1(EnConfigIO1), .out(multiplexer_1_out));
  D_FF_AS d_ff_as_1 (.Set(SConfig), .D(multiplexer_1_out), .C(Clock), .Clr(CConfig), .Q(SaConfigIO1));  // open: nQ
  Multiplexer multiplexer_2 (
    .sel(EnableEntradaSalida), .in_0(RegistroEntrada1), .in_1(InputIO1_t), .out(multiplexer_2_out));
  Multiplexer multiplexer_3 (
    .sel(EnableEntradaSalida), .in_0(OutputIO1_t), .in_1(DatoSalida1), .out(multiplexer_3_out));
  D_FF_AS d_ff_as_2 (
    .Set(SEntrada), .D(multiplexer_2_out), .C(Clock), .Clr(CEntrada), .Q(RegistroEntrada1));  // open: nQ
  D_FF_AS d_ff_as_3 (.Set(SEntrada), .D(multiplexer_3_out), .C(Clock), .Clr(CSalida), .Q(OutputIO1_t));  // open: nQ
  Multiplexer multiplexer_4 (.sel(EnConfig), .in_0(SaConfigIO2), .in_1(EnConfigIO2), .out(multiplexer_4_out));
  D_FF_AS d_ff_as_4 (.Set(SConfig), .D(multiplexer_4_out), .C(Clock), .Clr(CConfig), .Q(SaConfigIO2));  // open: nQ
  Multiplexer multiplexer_5 (
    .sel(EnableEntradaSalida), .in_0(RegistroEntrada2), .in_1(InputIO2_t), .out(multiplexer_5_out));
  Multiplexer multiplexer_6 (
    .sel(EnableEntradaSalida), .in_0(OutputIO2_t), .in_1(DatoSalida2), .out(multiplexer_6_out));
  D_FF_AS d_ff_as_5 (
    .Set(SEntrada), .D(multiplexer_5_out), .C(Clock), .Clr(CEntrada), .Q(RegistroEntrada2));  // open: nQ
  D_FF_AS d_ff_as_6 (.Set(SEntrada), .D(multiplexer_6_out), .C(Clock), .Clr(CSalida), .Q(OutputIO2_t));  // open: nQ
  Multiplexer multiplexer_7 (
    .sel(EnableEntradaSalida), .in_0(RegistroEntrada3), .in_1(InputIO3_t), .out(multiplexer_7_out));
  Multiplexer multiplexer_8 (
    .sel(EnableEntradaSalida), .in_0(OutputIO3_t), .in_1(DatoSalida2_2), .out(multiplexer_8_out));
  Multiplexer multiplexer_9 (.sel(EnConfig), .in_0(SaConfigIO3), .in_1(EnConfigIO3), .out(multiplexer_9_out));
  D_FF_AS d_ff_as_7 (.Set(SConfig), .D(multiplexer_9_out), .C(Clock), .Clr(CConfig), .Q(SaConfigIO3));  // open: nQ
  D_FF_AS d_ff_as_8 (
    .Set(SEntrada), .D(multiplexer_7_out), .C(Clock), .Clr(CEntrada), .Q(RegistroEntrada3));  // open: nQ
  D_FF_AS d_ff_as_9 (.Set(SEntrada), .D(multiplexer_8_out), .C(Clock), .Clr(CSalida), .Q(OutputIO3_t));  // open: nQ
  Multiplexer multiplexer_10 (
    .sel(EnableEntradaSalida), .in_0(RegistroEntrada4), .in_1(InputIO4_t), .out(multiplexer_10_out));
  Multiplexer multiplexer_11 (
    .sel(EnableEntradaSalida), .in_0(OutputIO4_t), .in_1(DatoSalida14), .out(multiplexer_11_out));
  D_FF_AS d_ff_as_10 (
    .Set(SEntrada), .D(multiplexer_10_out), .C(Clock), .Clr(CEntrada), .Q(RegistroEntrada4));  // open: nQ
  D_FF_AS d_ff_as_11 (.Set(SEntrada), .D(multiplexer_11_out), .C(Clock), .Clr(CSalida), .Q(OutputIO4_t));  // open: nQ
  Multiplexer multiplexer_12 (.sel(EnConfig), .in_0(SaConfigIO4), .in_1(EnConfigIO4), .out(multiplexer_12_out));
  D_FF_AS d_ff_as_12 (.Set(SConfig), .D(multiplexer_12_out), .C(Clock), .Clr(CConfig), .Q(SaConfigIO4));  // open: nQ

  assign SSalida = SEntrada;

  // Other names for the same wires on the sheet: CC = CConfig; CE = CEntrada; CS = CSalida; EnC = EnConfig;
  //   EnES = EnableEntradaSalida; SalConf1 = SaConfigIO1; SalConf2 = SaConfigIO2; SalConf3 = SaConfigIO3;
  //   SalConf4 = SaConfigIO4; SC = SConfig; SE = SEntrada

  // Notes on the sheet:
  //   Clock: Hz: 5
  //   Tri-State Buffer
  //   Entradas y Salidas del I/O
  //   Parte que se "comunica" con el exterior
  //   recibiendo o entregando datos.
  //   Entrada - Salida Pin
  //   Registro de Entradas
  //   Registro de Salidas
  //   Registro de Configuración
  //   Entrada 0, Salida 1
  //   Pequeña descripción de uso.
  //   Se puede ver que se tiene un 
  //   registro de configuración en el 
  //   cuál se maneja si el I/O se utiliza 
  //   como entrada o salida.
  //   Las entradas se dan en la parte 
  //   de Entrada - Salida Pin en los 
  //   InputIOX siendo X el número del IO
  //   y se guardaran "dentro" en la parte 
  //   de Registro EntradaX.
  //   Para las salidas los datos vendrán
  //   desde "dentro" por lo que se asignan
  //   desde dentro del registro en
  //   DatoSalidaX siendo X el numero del
  //   pin y su resultado se muestra en 
  //   Entrada -Salida Pin en los outputs.
  //   Cabe aclarar que para las entradas
  //   que por problema de tierra flotante
  //   cuando el multiplexor le requiere el
  //   dato al estado de alta impedancia,
  //   este le da un valor aleatorio entre 0
  //   y 1, logrando con esto que los valores
  //   en RegistroEntradaX cambien sin que
  //   se esté utilizando el pin como entrada.
  //   Esto solo sucede al utilizar el pin como
  //   salida.
endmodule
